# Fritzing sketch led-strip-single-channel (saved by Fritzing 0.9.0b)
stripboards: 1
breadboards: 1

parts:
  Q2 = Basic FET P-Channel [package="TO220 [THT]"]
  Part1 = Arduino Uno (Rev3)

nets:
  N1: Q2.gate, Part1.D9_PWM
  N2: Q2.source, Part1.GND
